# Fritzing sketch CoreElectronicsGroup1 (saved by Fritzing 0.9.3b)
circuit board: 13.3cm x 9.6cm
breadboards: 2

parts:
  FeatherM0 = Adafruit Feather M0 Basic Proto [part_number="Adafruit #2772"]
  Geiger1 = RJ11 Jack [package=rj11-6]
  Geiger2 = RJ11 Jack [package=rj11-6]
  GPS = COPERNICUS-DIP [package=copernicus-dip]
  Part3 = Adafruit TSL2561 [part_number="Adafruit #439"]  # not connected
  IMU = 9-DOF Absolute Orientation IMU Fusion Breakout - BNO055
  Part4 = Altitude/Pressure Sensor - MPL3115A2 Breakout [part_number=SEN-11084]  # not connected
  L1Power = Screw terminal - 2 pins [package=THT]
  L1Signal = Screw terminal - 2 pins [package=THT]
  L2Power = Screw terminal - 2 pins [package=THT]
  L2Signal = Screw terminal - 2 pins [package=THT]
  L3Signal = Screw terminal - 2 pins [package=THT]
  L3Power = Screw terminal - 2 pins [package=THT]
  PressureSensorPower = Screw terminal - 2 pins [package=THT]
  PressureSensorSignal = Screw terminal - 2 pins [package=THT]

nets:
  GND: FeatherM0.GND, Geiger1.5, Geiger2.5, GPS.OPEN, GPS.GND, IMU.GND, L1Power.pin1, L2Power.pin1, L3Power.pin1, PressureSensorPower.pin1
  N1: FeatherM0.D0, GPS.TXD-B
  +3V3: FeatherM0.+3V3, Geiger1.4, Geiger2.4, GPS.VCC, GPS.XSTANDBY, IMU.5.0V, L1Power.pin2, L2Power.pin2, L3Power.pin2, PressureSensorPower.pin2
  N2: FeatherM0.D12, Geiger2.3
  N3: FeatherM0.D11, Geiger1.3
  N4: FeatherM0.SCL, IMU.SCL_5V, L1Signal.pin1, L2Signal.pin1, L3Signal.pin1, PressureSensorSignal.pin1
  N5: FeatherM0.SDA, IMU.SDA_5V, L1Signal.pin2, L2Signal.pin2, L3Signal.pin2, PressureSensorSignal.pin2

custom parts:
  Adafruit Feather M0 Basic Proto: At the Feather M0's heart is an ATSAMD21G18 ARM Cortex M0 processor, clocked at 48 MHz and at 3.3V logic, the same one used in the new Arduino Zero. This chip has a whopping 256K of FLASH (8x more than the Atmega328 or 32u4) and 32K of RAM (16x as much)! This chip comes with built in USB so it has USB-to-Serial program & debug capability built in with no need for an FTDI-like chip. To make it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
  Adafruit TSL2561: The TSL2561 luminosity sensor is an advanced digital light sensor, ideal for use in a wide range of light situations. Compared to low cost CdS cells, this sensor is more precise, allowing for exact lux calculations and can be configured for different gain/timing ranges to detect light ranges from up to 0.1 - 40,000+ Lux on the fly. The best part of this sensor is that it contains both infrared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
  9-DOF Absolute Orientation IMU Fusion Breakout - BNO055: A MEMS accelerometer, magnetometer and gyroscope on a single die with a high speed ARM Cortex-M0 based processor to digest all the sensor data, abstract the sensor fusion and real time requirements away, and spit out data you can use in quaternions, Euler angles or vectors.
